// Logisim project control_logic.circ as structural Verilog: 1 circuit, main circuit control_logic
module control_logic (
  input  [31:0] inst,
  input  BrEq,
  input  BrLt,
  output PCSel,
  output RegWEn,
  output [2:0] ImmSel,
  output BrUn,
  output ASel,
  output BSel,
  output [3:0] ALUSel,
  output [3:0] MemRW,
  output [1:0] WBSel,
  output CSRSel,
  output CSRWen
);

  wire add, add_mul_sub, addi, ALUSel0_I_N, ALUSel0_LUI, ALUSel0_R, ALUSel1_I_N, ALUSel1_R, ALUSel2_I_N,
       ALUSel2_R, ALUSel3_R, and_1_out, and_2_out, and_3_out, and_4_out, and_5_out, and_6_out, andd, AUPIC,
       beq, bge, bgeu, blt, bltu, bne, I_Type_Normal, mul, mulh, mulhu, ori, orr, R_Type, S_Type, SB_Type,
       sh, sll_mulh, slli, slll, slt, slti, sraa, srai, srl_sra, srli, srli_srai, srll, sub, sw, xori, xorr;

  Demultiplexer #(.enable("false"), .select(5)) demultiplexer_1 (
    .out4(I_Type_Normal), .out5(AUPIC), .out7(S_Type), .out12(R_Type), .out13(ALUSel0_LUI), .out24(SB_Type),
    .out27(ImmSel[2]), .in(1'b1), .sel(inst[6:2]));  // open: out0, out1, out2, out3, out6, out8, out9, out10, out11, out14, out15, out16, out17, out18, out19, out20, out21, out22, out23, out25, out26, out28, out29, out30, out31
  Demultiplexer #(.enable("false"), .select(3)) demultiplexer_2 (
    .out0(MemRW[3]), .out1(sh), .out2(sw), .in(S_Type), .sel(inst[14:12]));  // open: out3, out4, out5, out6, out7
  Demultiplexer #(.enable("false"), .select(3)) demultiplexer_3 (
    .out0(beq), .out1(bne), .out4(blt), .out5(bge), .out6(bltu), .out7(bgeu), .in(SB_Type), .sel(inst[14:12]));  // open: out2, out3
  or or_1 (ASel, SB_Type, ImmSel[2], AUPIC);
  Demultiplexer #(.enable("false"), .select(3)) demultiplexer_4 (
    .out0(add_mul_sub), .out1(sll_mulh), .out2(slt), .out3(mulhu), .out4(xorr), .out5(srl_sra), .out6(orr),
    .out7(andd), .in(R_Type), .sel(inst[14:12]));
  Demultiplexer #(.enable("false"), .select(3)) demultiplexer_5 (
    .out0(addi), .out1(slli), .out2(slti), .out4(xori), .out5(srli_srai), .out6(ori), .in(I_Type_Normal),
    .sel(inst[14:12]));  // open: out3, out7
  or or_2 (BSel, ALUSel0_LUI, I_Type_Normal, SB_Type, S_Type, AUPIC, ImmSel[2]);
  or or_3 (RegWEn, R_Type, AUPIC, ImmSel[2], ALUSel0_LUI, I_Type_Normal);
  or or_4 (WBSel[0], R_Type, AUPIC, ALUSel0_LUI, I_Type_Normal);
  Demultiplexer #(.enable("false"), .select(2)) demultiplexer_6 (
    .out0(add), .out1(mul), .out2(sub), .in(add_mul_sub), .sel({inst[30], inst[25]}));  // open: out3
  or or_5 (ALUSel3_R, mul, sub, mulh, mulhu);
  or or_6 (ALUSel2_R, sub, srll, sraa, slll, slt, mulh);
  or or_7 (ALUSel2_I_N, srli, srai, slli, slti);
  Demultiplexer #(.enable("false")) demultiplexer_7 (.out0(slll), .out1(mulh), .in(sll_mulh), .sel(inst[25]));
  or or_8 (ALUSel1_R, orr, xorr, slll, mulh, slt, mul, mulh);
  or or_9 (ALUSel1_I_N, ori, xori, slli, slti);
  or or_10 (ALUSel0_R, andd, xorr, sraa, slt, mulhu);
  or or_11 (ALUSel0_I_N, slti, srai, xori);
  Demultiplexer #(.enable("false")) demultiplexer_8 (.out0(srll), .out1(sraa), .in(srl_sra), .sel(inst[30]));
  or or_12 (ALUSel[3], ALUSel3_R, 1'b0, ALUSel0_LUI);
  or or_13 (ALUSel[2], ALUSel2_R, ALUSel2_I_N, ALUSel0_LUI);
  Demultiplexer #(.enable("false")) demultiplexer_9 (.out0(srli), .out1(srai), .in(srli_srai), .sel(inst[30]));
  or or_14 (ALUSel[1], ALUSel1_R, ALUSel1_I_N, 1'b0);
  or or_15 (ALUSel[0], ALUSel0_R, ALUSel0_I_N, ALUSel0_LUI);
  or or_16 (ImmSel[1], SB_Type, ALUSel0_LUI, AUPIC);
  or or_17 (ImmSel[0], S_Type, ALUSel0_LUI, AUPIC);
  and and_1 (and_1_out, beq, BrEq);
  and and_2 (and_2_out, bne, ~BrEq);  // AND_Gate
  or or_18 (PCSel, and_1_out, and_2_out, ImmSel[2], and_3_out, and_4_out, and_5_out, and_6_out);
  and and_3 (and_3_out, blt, BrLt);
  and and_4 (and_4_out, bge, ~BrLt);  // AND_Gate
  and and_5 (and_5_out, bltu, BrLt);
  and and_6 (and_6_out, bgeu, ~BrLt);  // AND_Gate
  or or_19 (BrUn, bltu, bgeu);
  or or_20 (MemRW[1], sh, sw);
  or or_21 (MemRW[0], MemRW[3], sh, sw);

  assign MemRW[2] = MemRW[3];
  assign WBSel[1] = ImmSel[2];

  // Other names for the same wires on the sheet: func7low = inst[25]; func7high = inst[30]; UJ_Type = ImmSel[2];
  //   WBSel_1 = ImmSel[2]; func3[2:0] = inst[14:12]; ALUSel2_LUI = ALUSel0_LUI; ALUSel3_LUI = ALUSel0_LUI;
  //   LUI = ALUSel0_LUI; sb = MemRW[3]; WBSel_0 = WBSel[0]

  // Notes on the sheet:
  //   INPUTS to your circuit
  //   DON'T CHANGE THE LOCATIONS OF THE INPUTS AND OUTPUTS!
  //   OUTPUT from your circuit
  //   add/mul/sub
  //   add/mul/sub
  //   and
  //   sll/mulh
  //   or
  //   or
  //   slt
  //   srl/sra
  //   srl/sra
  //   mulhu
  //   xor
  //   xor
endmodule
